# Fritzing sketch Fritzing - Phepooyans 147 (saved by Fritzing 0.9.3b)
breadboards: 1

parts:
  Raspberry_Pi_2 = Raspberry Pi 3 [part_number=RPI-3-V1.2]
  F2 = Fan - Ventilador [package=THT]
  YL-83_-_Control_Board2 = YL-83 Rain Sensor - Control Board
  YL-83_-_Detection_Board2 = YL-83 Rain Sensor - Detection Board
  Часть3 = BH1750
  DHT2 = Humidity and Temperature Sensor DHT11
  J5 = Piezo Speaker
  J6 = Basic Servo
  KY-1 = Keyes Relay [package=THT]
  F3 = Fan - Ventilador [package=THT]
  Part3 = Lilypad Battery Connect

nets:
  VCC: Raspberry_Pi_2.3v3, Raspberry_Pi_2.3V3, YL-83_-_Control_Board2.VCC, Часть3.VCC, DHT2.Vcc
  N1: Raspberry_Pi_2.GPIO2, Часть3.SDA
  GND: Raspberry_Pi_2.GPIO3, Raspberry_Pi_2.GND, F2.GND, YL-83_-_Control_Board2.GND, Часть3.GND, Часть3.SCL, DHT2.GND_1, J5.pin1, J6.gnd, KY-1.ground
  N2: Raspberry_Pi_2.GPIO4, DHT2.Data-signal
  N3: Raspberry_Pi_2.GPIO17, YL-83_-_Control_Board2.AO
  N4: Raspberry_Pi_2.GPIO13, KY-1.signal
  N5: Raspberry_Pi_2.GPIO23, J6.pulse
  N6: Raspberry_Pi_2.GPIO18, J5.pin2
  5V: Raspberry_Pi_2.5V, F2.5V, J6.vcc, KY-1.power
  N7: YL-83_-_Control_Board2.POS, YL-83_-_Detection_Board2.POS
  N8: YL-83_-_Control_Board2.NEG, YL-83_-_Detection_Board2.NEG
  N9: KY-1.C, KY-1.NO, F3.5V, Part3.-
  N10: F3.GND, Part3.+

custom parts:
  Fan - Ventilador: Ventilador de 2 pines, se encuentra comunmente en computadoras de escritorio
  YL-83 Rain Sensor - Control Board: The YL-83 is a rain sensor that has more resistance when dry and less resistance when wet. The module runs at 5V.
  YL-83 Rain Sensor - Detection Board: The YL-83 is a rain sensor that has more resistance when dry and less resistance when wet. The module runs at 5V.
  BH1750: Light Sensor
  Humidity and Temperature Sensor DHT11: Digital relative humidity & temperature sensor DHT11
  Keyes Relay: The Keyes 5V relay module is suitable for SCM development, home appliance control. It uses a 5V~12V TIL control signal which can control DC / AC signal.
